# Fritzing sketch ir_blaster (saved by Fritzing 0.9.3b)
breadboards: 1

parts:
  U1 = NodeMCU V1.0
  IR1 = TSOP312.., 314.. [package=THT]
  R1 = Resistor [tolerance=±5% resistance=100 package=THT]
  LED1 = LED - 5mm [color="Infrared (940nm)" package="5 mm [THT]"]
  Q1 = NPN-Transistor [package="TO92 [THT]"]

nets:
  N1: U1.D0, Q1.B
  N2: U1.D1, IR1.Data
  N3: U1.3V3, R1.Pin_0
  GND: U1.GND, IR1.GND, Q1.E
  N4: U1.Vin, LED1.cathode
  N5: IR1.Vs, R1.Pin_1
  N6: LED1.anode, Q1.C

custom parts:
  NodeMCU V1.0: ESP9266 based NodeMCU
